# Fritzing sketch dojo_watcher_semaphore (saved by Fritzing 0.8.7b)
breadboards: 1

parts:
  Componente1 = Arduino Uno (Rev3)
  LED1 = LED - 5mm [color="Red (633nm)" package="5 mm [THT]"]
  LED2 = LED - 5mm [color="Green (565nm)" package="5 mm [THT]"]
  R1 = Resistor [tolerance=±5% resistance=220 package=THT]
  R2 = Resistor [tolerance=±5% resistance=220 package=THT]

nets:
  N1: Componente1.D2, LED1.cathode
  N2: Componente1.D3_PWM, LED2.cathode
  N3: Componente1.GND, R1.Pin_1, R2.Pin_1
  N4: LED1.anode, R1.Pin_0
  N5: LED2.anode, R2.Pin_0

notes:
  Mais pra frente, alem dos leds, um RELE "pra cada led". ai poderemos acender uma lampada
